# Fritzing sketch breadboard (saved by Fritzing 0.9.3b)
breadboards: 1

parts:
  R1 = Photocell (LDR) [package=THT]
  C1 = Electrolytic Capacitor [capacitance=1µF package="100 mil [THT, electrolytic]"]
  Part1 = Adafruit Pi Cobbler Plus [part_number="Adafruit #2029"]

nets:
  N1: R1.pin_0, Part1.+3.3V
  N2: R1.pin_1, C1.-, Part1.GPIO4
  N3: C1.+, Part1.GND

custom parts:
  Adafruit Pi Cobbler Plus: The Raspberry Pi B+/Pi 2/ Pi 3 has landed on the Maker World like a 40-GPIO pinned, quad-USB ported, credit card sized bomb of DIY joy. And while you can use most of our great Model B accessories by hooking up our downgrade cable, its probably a good time to upgrade your set up and accessorize using all of the Model B+'s / Pi 2's / Pi 3's 40 pins. That's why we now carry the Adafruit Assembled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
