# Fritzing sketch breadboard-ultrasonidos-led (saved by Fritzing 0.9.3b)
breadboards: 1

parts:
  Part5 = Adafruit Pi Cobbler Plus [part_number="Adafruit #2029"]
  hc-sr1 = hc-sr04
  R1 = Resistor [tolerance=±5% resistance=330 package=THT]
  R2 = Resistor [tolerance=±5% resistance=470 package=THT]
  LED1 = LED - 5mm [color="Red (633nm)" package="5 mm [THT]"]
  R3 = Resistor [tolerance=±5% resistance=220 package=THT]

nets:
  GND: Part5.GND, hc-sr1.GND, R2.Pin_1, LED1.cathode
  N1: Part5.GPIO20, R3.Pin_1
  +5V: Part5.+5V, hc-sr1.VCC
  N2: Part5.GPIO4, hc-sr1.Trig
  N3: Part5.GPIO17, R1.Pin_1, R2.Pin_0
  N4: hc-sr1.Echo, R1.Pin_0
  N5: LED1.anode, R3.Pin_0

custom parts:
  Adafruit Pi Cobbler Plus: The Raspberry Pi B+/Pi 2/ Pi 3 has landed on the Maker World like a 40-GPIO pinned, quad-USB ported, credit card sized bomb of DIY joy. And while you can use most of our great Model B accessories by hooking up our downgrade cable, its probably a good time to upgrade your set up and accessorize using all of the Model B+'s / Pi 2's / Pi 3's 40 pins. That's why we now carry the Adafruit Assembled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
