# Fritzing sketch breadboard-rgb (saved by Fritzing 0.9.3b)
breadboards: 1

parts:
  Part1 = Adafruit Pi Cobbler Plus [part_number="Adafruit #2029"]
  Part2 = KY-009 Full Color RGB LED SMD Module [package="Breakout board"]
  R1 = Resistor [tolerance=±5% resistance=220 package=THT]

nets:
  N1: Part1.GND, R1.Pin_1
  N2: Part1.EEDAT, Part1.GPIO5, Part2.B
  N3: Part1.GPIO6, Part2.G
  N4: Part1.GPIO13, Part2.R
  N5: Part2.-, R1.Pin_0

custom parts:
  Adafruit Pi Cobbler Plus: The Raspberry Pi B+/Pi 2/ Pi 3 has landed on the Maker World like a 40-GPIO pinned, quad-USB ported, credit card sized bomb of DIY joy. And while you can use most of our great Model B accessories by hooking up our downgrade cable, its probably a good time to upgrade your set up and accessorize using all of the Model B+'s / Pi 2's / Pi 3's 40 pins. That's why we now carry the Adafruit Assembled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
  KY-009 Full Color RGB LED SMD Module: RGB full color LED Module KY-009 for Arduino, emits a range of colors by mixing red, green and blue. The amount of each primary color is adjusted using PWM.
