# Fritzing sketch breadboard-rele-led-gpio (saved by Fritzing 0.9.3b)
breadboards: 1

parts:
  Part2 = Adafruit Pi Cobbler Plus [part_number="Adafruit #2029"]
  R1 = Resistor [tolerance=±5% resistance=220 package=THT]
  LED1 = LED - 5mm [color="Red (633nm)" package="5 mm [THT]"]
  KY-1 = Keyes Relay [package=THT]
  VCC1 = Battery

nets:
  N1: Part2.+3.3V, KY-1.power
  N2: Part2.GND, KY-1.ground
  N3: Part2.GPIO24, KY-1.signal
  N4: R1.Pin_0, LED1.anode
  N5: R1.Pin_1, VCC1.-
  N6: LED1.cathode, KY-1.C
  N7: KY-1.NO, VCC1.+

custom parts:
  Adafruit Pi Cobbler Plus: The Raspberry Pi B+/Pi 2/ Pi 3 has landed on the Maker World like a 40-GPIO pinned, quad-USB ported, credit card sized bomb of DIY joy. And while you can use most of our great Model B accessories by hooking up our downgrade cable, its probably a good time to upgrade your set up and accessorize using all of the Model B+'s / Pi 2's / Pi 3's 40 pins. That's why we now carry the Adafruit Assembled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
  Keyes Relay: The Keyes 5V relay module is suitable for SCM development, home appliance control. It uses a 5V~12V TIL control signal which can control DC / AC signal.
