# Fritzing sketch breadboard-led-abierto (saved by Fritzing 0.9.3b)
breadboards: 1

parts:
  R1 = Resistor [tolerance=±5% resistance=220 package=THT]
  KY-2 = Keyes Relay [package=THT]  # not connected
  VCC1 = Battery
  LED1 = LED - 3mm [color="Red (633nm)" package="3 mm [THT]"]

nets:
  N1: R1.Pin_0, LED1.anode
  N2: R1.Pin_1, VCC1.-

custom parts:
  Keyes Relay: The Keyes 5V relay module is suitable for SCM development, home appliance control. It uses a 5V~12V TIL control signal which can control DC / AC signal.
